# Fritzing sketch JR Gamepad Module Stripboard (saved by Fritzing 0.9.4)
stripboards: 1

parts:
  U1 = Voltage Regulator - 3.3V [package="TO220 [THT]"]
  J1 = female pin header, 5 pins [form="♀ (female)"]
  R2 = Resistor [tolerance=±5% resistance=330 package=THT]
  S1 = Toggle Switch [package=THT]
  R3 = Resistor [tolerance=±5% resistance=15k package=THT]
  Q1 = NPN-Transistor [package="TO92 [THT]"]
  C1 = Capacitor Polarized [package=panasonic_c]
  R1 = Resistor [tolerance=±5% resistance=47k package=THT]
  ESP32_D1_Mini = MH-ET Live Minikit for ESP32

nets:
  N1: U1.input_voltage, S1.COM
  GND: U1.GND, J1.pin2, R2.Pin_0, C1.-, ESP32_D1_Mini.GND
  N2: U1.output_voltage, R3.Pin_0, C1.+, ESP32_D1_Mini.3.3V
  N3: J1.pin3, S1.L2
  N4: J1.pin5, R1.Pin_0
  N5: R2.Pin_1, Q1.E
  N6: R3.Pin_1, Q1.C, ESP32_D1_Mini.IO22
  N7: Q1.B, R1.Pin_1

notes:
  Notes:
  - This stripboard layout fits the "DIY box" found in Jumper transmitters.
  - Use the "Layers" window to only display the board, as there are quite a few strips to be cut, and others to be joined.
  - The JR module bay has 5 long protruding pins, requiring to dremel/cut the lower left corner of the stripboard, then fitting something like a Molex 22-14-2054 board connector for proper interfacing (but a simple, straight 5-pin female header with its pins bent 180° will work just as well ;-)
  Depending on the type and size of your connector you may have to dremel the lower right corner of the ESP32 board's PCB to make it fit. That's not an issue because that part of the PCB is nearly transparent (It does not feature any traces)
  - The 3.3V regulator has to be mounted to the back of the board, as things are a bit tight on top.
  - Check your particular transistor's pin layout! The stripboard assumes a C-B-E layout.
  - Unused strips are grounded on purpose to make the board act as a ground plane. Join adjacent stripes with blobs of solder.
  - The on/off switch is meant to be fitted to the module's plastic top cover.
  - By a strange coincidence, the location of the screw holes line up exactly with the 3rd stripboard hole in the top row, and the 4th hole in the bottom row (counting from the right)

custom parts:
  MH-ET Live Minikit for ESP32: MH-ET Live Minikit for ESP32 ( http://mh.nodebb.com/topic/8/mh-et-live-minikit-for-esp32/2/) PCB footprint is invalid.
